// Logisim project ALU.circ as structural Verilog: 2 circuits, main circuit one bit Alu
module one_bit_Alu (
  input  [2:0] OP,
  input  Sub,
  input  Cin,
  input  A,
  input  B,
  input  LESS,
  output RESULT,
  output Cout,
  output SET
);

  wire and_1_out, multiplexer_1_out, nor_1_out, or_1_out, xor_1_out;

  and and_1 (and_1_out, A, B);
  or or_1 (or_1_out, A, B);
  Multiplexer multiplexer_1 (.in0(B), .in1(B), .out(multiplexer_1_out), .sel(Sub));  // open: en
  xor xor_1 (xor_1_out, A, B);
  nor nor_1 (nor_1_out, A, B);
  Adder #(.width(1)) adder_1 (.a(A), .b(multiplexer_1_out), .out(SET), .cin(Cin), .cout(Cout));
  Multiplexer #(.select(3)) multiplexer_2 (
    .in0(and_1_out), .in1(or_1_out), .in2(xor_1_out), .in3(nor_1_out), .in4(SET), .in5(LESS), .out(RESULT),
    .sel(OP));  // open: in6, in7, en
endmodule

module ALU (
  input  [2:0] Op,
  input  in_2,
  input  [7:0] A,
  input  [7:0] B,
  output [7:0] out_5,
  output Zero
);

  wire one_bit_alu_1_set, one_bit_alu_2_set, one_bit_alu_3_set, one_bit_alu_4_set, one_bit_alu_5_set,
       one_bit_alu_6_set, one_bit_alu_7_set, one_bit_alu_8_cout;

  one_bit_Alu one_bit_alu_1 (
    .OP(Op), .Sub(in_2), .A(A[0]), .B(B[0]), .LESS(one_bit_alu_8_cout), .RESULT(out_5[0]),
    .SET(one_bit_alu_1_set), .Cin(in_2));  // open: Cout
  one_bit_Alu one_bit_alu_2 (
    .OP(Op), .Sub(in_2), .A(A[1]), .B(B[1]), .LESS(1'b0), .RESULT(out_5[1]), .SET(one_bit_alu_2_set),
    .Cin(one_bit_alu_1_set));  // open: Cout
  one_bit_Alu one_bit_alu_3 (
    .OP(Op), .Sub(in_2), .A(A[3]), .B(B[2]), .LESS(1'b0), .RESULT(out_5[2]), .SET(one_bit_alu_3_set),
    .Cin(one_bit_alu_2_set));  // open: Cout
  one_bit_Alu one_bit_alu_4 (
    .OP(Op), .Sub(in_2), .A(A[2]), .B(B[3]), .LESS(1'b0), .RESULT(out_5[3]), .SET(one_bit_alu_4_set),
    .Cin(one_bit_alu_3_set));  // open: Cout
  one_bit_Alu one_bit_alu_5 (
    .OP(Op), .Sub(in_2), .A(A[4]), .B(B[4]), .LESS(1'b0), .RESULT(out_5[4]), .SET(one_bit_alu_5_set),
    .Cin(one_bit_alu_4_set));  // open: Cout
  one_bit_Alu one_bit_alu_6 (
    .OP(Op), .Sub(in_2), .A(A[5]), .B(B[5]), .LESS(1'b0), .RESULT(out_5[5]), .SET(one_bit_alu_6_set),
    .Cin(one_bit_alu_5_set));  // open: Cout
  one_bit_Alu one_bit_alu_7 (
    .OP(Op), .Sub(in_2), .A(A[6]), .B(B[6]), .LESS(1'b0), .RESULT(out_5[6]), .SET(one_bit_alu_7_set),
    .Cin(one_bit_alu_6_set));  // open: Cout
  one_bit_Alu one_bit_alu_8 (
    .OP(Op), .Sub(in_2), .A(A[7]), .B(B[7]), .LESS(1'b0), .RESULT(out_5[7]), .Cout(one_bit_alu_8_cout),
    .Cin(one_bit_alu_7_set));  // open: SET
  nor nor_1 (Zero, out_5[7], out_5[6], out_5[5], out_5[4], out_5[3], out_5[2], out_5[1], out_5[0]);
endmodule
