// Logisim project D-flip flop.circ as structural Verilog: 1 circuit, main circuit main
module main (
  output out_1,
  output out_2,
  output out_3,
  output out_4,
  output out_5,
  output out_6,
  output out_7,
  output out_8
);

  wire nand_1_out, nand_2_out, nand_3_out, nand_4_out, nand_5_out, nand_6_out, nand_7_out, nand_8_out,
       nand_9_out, nand_10_out, nand_11_out, nand_12_out, nand_13_out, nand_14_out, nand_15_out, nand_16_out,
       nand_17_out, nand_18_out, nand_19_out, nand_24_out, nand_25_out, nand_26_out, nand_27_out;

  nand nand_1 (nand_1_out, 1'b1, 1'b0);
  nand nand_2 (nand_2_out, nand_1_out, 1'b0);
  nand nand_3 (nand_3_out, 1'b0, 1'b0);
  nand nand_4 (nand_4_out, nand_1_out, nand_5_out);
  nand nand_5 (nand_5_out, nand_4_out, nand_2_out);
  nand nand_6 (nand_6_out, 1'b0, 1'b0);
  nand nand_7 (nand_7_out, 1'b1, 1'b1);
  nand nand_8 (nand_8_out, 1'b1, nand_3_out);
  nand nand_9 (nand_9_out, nand_8_out, nand_3_out);
  nand nand_10 (nand_10_out, 1'b0, nand_7_out);
  nand nand_11 (nand_11_out, nand_10_out, nand_7_out);
  nand nand_12 (nand_12_out, 1'b0, 1'b0);
  nand nand_13 (nand_13_out, nand_12_out, 1'b0);
  nand nand_14 (nand_14_out, nand_4_out, nand_6_out);
  nand nand_15 (nand_15_out, nand_14_out, nand_6_out);
  nand nand_16 (nand_16_out, nand_8_out, nand_17_out);
  nand nand_17 (nand_17_out, nand_16_out, nand_9_out);
  nand nand_18 (nand_18_out, nand_10_out, nand_19_out);
  nand nand_19 (nand_19_out, nand_18_out, nand_11_out);
  nand nand_20 (out_1, nand_12_out, out_2);
  nand nand_21 (out_2, out_1, nand_13_out);
  nand nand_22 (out_3, nand_14_out, out_4);
  nand nand_23 (out_4, out_3, nand_15_out);
  nand nand_24 (nand_24_out, nand_16_out, 1'b0);
  nand nand_25 (nand_25_out, nand_24_out, 1'b0);
  nand nand_26 (nand_26_out, nand_18_out, 1'b1);
  nand nand_27 (nand_27_out, nand_26_out, 1'b1);
  nand nand_28 (out_7, nand_24_out, out_8);
  nand nand_29 (out_8, out_7, nand_25_out);
  nand nand_30 (out_5, nand_26_out, out_6);
  nand nand_31 (out_6, out_5, nand_27_out);

  // Notes on the sheet:
  //   FALLING
  //   RISING
  //   D-latch
endmodule
