// Logisim project OnCourseWed.circ as structural Verilog: 1 circuit, main circuit main
module main (
  output out_1,
  output out_2
);

  wire transistor_1_out, transistor_7_out, transistor_9_out, transistor_11_out, transistor_16_out;

  Transistor transistor_1 (.in(1'b1), .out(transistor_1_out), .gate(1'b0));
  Transistor #(.\type ("n")) transistor_2 (.in(1'b0), .out(transistor_1_out), .gate(1'b0));
  Transistor transistor_3 (.in(1'b1), .out(out_1), .gate(1'b0));
  Transistor #(.\type ("n")) transistor_4 (.in(1'b0), .out(out_1), .gate(1'b0));
  Transistor transistor_5 (.in(1'b1), .out(out_1), .gate(out_1));
  Transistor #(.\type ("n")) transistor_6 (.in(transistor_7_out), .out(out_1), .gate(out_1));
  Transistor #(.\type ("n")) transistor_7 (.in(1'b0), .out(transistor_7_out), .gate(transistor_1_out));
  Transistor transistor_8 (.in(1'b1), .out(out_1), .gate(transistor_1_out));
  Transistor transistor_9 (.in(1'b1), .out(transistor_9_out), .gate(transistor_1_out));
  Transistor #(.\type ("n")) transistor_10 (.in(transistor_11_out), .out(transistor_9_out), .gate(transistor_1_out));
  Transistor #(.\type ("n")) transistor_11 (.in(1'b0), .out(transistor_11_out), .gate(1'b0));
  Transistor transistor_12 (.in(1'b1), .out(transistor_9_out), .gate(1'b0));
  Transistor transistor_13 (.in(1'b1), .out(out_1), .gate(out_1));
  Transistor transistor_14 (.in(1'b1), .out(out_1), .gate(transistor_9_out));
  Transistor #(.\type ("n")) transistor_15 (.in(transistor_16_out), .out(out_1), .gate(out_1));
  Transistor #(.\type ("n")) transistor_16 (.in(1'b0), .out(transistor_16_out), .gate(transistor_9_out));

  assign out_2 = out_1;
endmodule
