// Logisim project SR JK.circ as structural Verilog: 1 circuit, main circuit main
module main (
  input  in_1,
  input  in_2,
  input  in_3,
  input  in_4,
  input  in_5,
  input  in_6,
  input  in_7,
  input  in_8,
  input  in_9,
  input  in_10,
  output out_11,
  output out_12,
  output out_13,
  output out_14,
  output out_15,
  output out_16,
  output out_17,
  output out_18,
  output out_19,
  output out_20,
  output out_21,
  output out_22,
  output out_23,
  output out_24
);

  wire clock_1_out, clock_2_out, clock_3_out, clock_4_out, clock_5_out, d_ff_1_q, d_ff_2_q, nand_1_out,
       nand_2_out, nand_3_out, nand_4_out, nand_7_out, nand_10_out, nand_11_out, nand_12_out, nand_13_out,
       nand_14_out, nand_15_out, nand_22_out, nand_23_out, nand_24_out, nand_25_out, nand_26_out;

  Clock clock_1 (.out(clock_1_out));
  Clock clock_2 (.out(clock_2_out));
  nand nand_1 (nand_1_out, in_5, clock_2_out);
  nand nand_2 (nand_2_out, clock_2_out, in_6);
  nand nand_3 (nand_3_out, in_1, clock_1_out);
  nand nand_4 (nand_4_out, clock_1_out, in_3);
  Clock clock_3 (.out(clock_3_out));
  nand nand_5 (out_15, nand_1_out, out_16);
  nand nand_6 (out_16, out_15, nand_2_out);
  nand nand_7 (nand_7_out, clock_3_out, clock_3_out);
  nand nand_8 (out_11, nand_3_out, out_13);
  nand nand_9 (out_13, out_11, nand_4_out);
  Clock clock_4 (.out(clock_4_out));
  Clock clock_5 (.out(clock_5_out));
  nand nand_10 (nand_10_out, out_19, in_7, clock_4_out);
  nand nand_11 (nand_11_out, clock_4_out, in_8, out_18);
  nand nand_12 (nand_12_out, out_23, in_9, nand_7_out);
  nand nand_13 (nand_13_out, nand_7_out, in_10, out_22);
  D_Flip_Flop d_ff_1 (.clk(clock_5_out), .D(out_14), .Q(d_ff_1_q));  // open: Qn, preset, en, reset
  nand nand_14 (nand_14_out, d_ff_1_q, in_2, clock_5_out);
  nand nand_15 (nand_15_out, clock_5_out, in_4, d_ff_2_q);
  D_Flip_Flop d_ff_2 (.clk(clock_5_out), .D(out_12), .Q(d_ff_2_q));  // open: Qn, preset, en, reset
  nand nand_16 (out_17, nand_10_out, out_20);
  nand nand_17 (out_20, out_17, nand_11_out);
  nand nand_18 (out_21, nand_12_out, out_24);
  nand nand_19 (out_24, out_21, nand_13_out);
  nand nand_20 (out_12, nand_14_out, out_14);
  nand nand_21 (out_14, out_12, nand_15_out);
  nand nand_22 (nand_22_out, clock_4_out, clock_4_out);
  nand nand_23 (nand_23_out, out_21, clock_3_out);
  nand nand_24 (nand_24_out, clock_3_out, out_24);
  nand nand_25 (nand_25_out, out_17, nand_22_out);
  nand nand_26 (nand_26_out, nand_22_out, out_20);
  nand nand_27 (out_18, nand_25_out, out_19);
  nand nand_28 (out_19, out_18, nand_26_out);
  nand nand_29 (out_22, nand_23_out, out_23);
  nand nand_30 (out_23, out_22, nand_24_out);

  // Notes on the sheet:
  //   SR FLIP FLOP
  //   Rising Edge
  //   Only change when clk is high
  //   Falling Edge
endmodule
