// Logisim project cmos.circ as structural Verilog: 1 circuit, main circuit main
module main (
  output out_1,
  output out_2,
  output out_3
);

  wire transistor_1_out, transistor_4_out, transistor_7_out, transistor_9_out, transistor_14_out;

  Transistor transistor_1 (.in(1'b1), .out(transistor_1_out), .gate(1'b0));
  Transistor transistor_2 (.in(transistor_1_out), .out(out_2), .gate(1'b0));
  Transistor #(.\type ("n")) transistor_3 (.in(1'b0), .out(out_2), .gate(1'b0));
  Transistor transistor_4 (.in(1'b1), .out(transistor_4_out), .gate(1'b1));
  Transistor #(.\type ("n")) transistor_5 (.in(1'b0), .out(transistor_4_out), .gate(1'b1));
  Transistor #(.\type ("n")) transistor_6 (.in(1'b0), .out(out_2), .gate(1'b0));
  // Probe on transistor_4_out
  Transistor #(.\type ("n")) transistor_7 (.in(1'b1), .out(transistor_7_out), .gate(1'b1));
  Transistor #(.\type ("n")) transistor_8 (.in(transistor_7_out), .out(out_1), .gate(1'b1));
  Transistor transistor_9 (.in(out_1), .out(transistor_9_out), .gate(1'b1));
  Transistor transistor_10 (.in(1'b1), .out(out_3), .gate(1'b1));
  Transistor transistor_11 (.in(out_1), .out(transistor_9_out), .gate(1'b1));
  Transistor transistor_12 (.in(1'b1), .out(out_3), .gate(1'b1));
  Transistor #(.\type ("n")) transistor_13 (.in(transistor_14_out), .out(out_3), .gate(1'b1));
  Transistor #(.\type ("n")) transistor_14 (.in(1'b0), .out(transistor_14_out), .gate(1'b1));
  // also tied to GND on the sheet: transistor_9_out

  // Notes on the sheet:
  //   not
  //   nor
  //   and
  //   nand
endmodule
