// Logisim project firstpt.circ as structural Verilog: 1 circuit, main circuit main
module main (
  output out_1
);

  wire nand_1_out, nand_2_out, nand_3_out, nand_4_out, nand_5_out, nand_6_out;

  nand nand_1 (nand_1_out, 1'b1, 1'b1);
  nand nand_2 (nand_2_out, 1'b0, 1'b0);
  nand nand_3 (nand_3_out, 1'b1, nand_1_out);
  nand nand_4 (nand_4_out, 1'b1, nand_2_out);
  nand nand_5 (nand_5_out, nand_1_out, 1'b0);
  nand nand_6 (nand_6_out, nand_3_out, nand_4_out);
  nand nand_7 (out_1, nand_6_out, nand_5_out);

  // Notes on the sheet:
  //   A
  //   B
  //   C
  //   D
endmodule
