// Logisim project full adder from nand.circ as structural Verilog: 1 circuit, main circuit main
module main (
  input  in_1,
  input  in_2,
  input  in_3,
  input  in_4,
  input  in_5,
  input  in_6,
  input  in_7,
  input  in_8,
  input  in_9,
  input  A,
  input  B,
  input  C,
  output out_13,
  output out_14,
  output out_15,
  output out_16,
  output out_17,
  output out_18,
  output out_19,
  output out_20,
  output out_21,
  output out_22,
  output out_23,
  output out_24,
  output out_25,
  output out_26,
  output out_27,
  output out_28,
  output out_29,
  output out_30,
  output out_31,
  output out_32,
  output out_33,
  output out_34,
  output out_35,
  output out_36
);

  wire A1_out, A2_out, A3_out, A4_out, A5_out, A6_out, A7_out, and_1_out, and_2_out, clock_1_out, d_ff_1_q,
       multiplexer_2_out, multiplexer_3_out, multiplexer_4_out, multiplexer_5_out, multiplexer_6_out,
       multiplexer_7_out, multiplexer_8_out, multiplexer_9_out, nand_1_out, nand_2_out, nand_3_out,
       nand_5_out, nand_6_out, nand_7_out, not_1_out, not_2_out, not_3_out, not_4_out, not_5_out, not_6_out,
       not_7_out, not_8_out, not_9_out, not_10_out, not_11_out, xor_1_out;

  Multiplexer #(.select(2)) multiplexer_1 (
    .in0(1'b1), .in1(1'b1), .in2(1'b1), .in3(1'b0), .out(out_22), .sel(2'b11));  // open: en
  nand nand_1 (nand_1_out, in_1, in_2);
  xor xor_1 (xor_1_out, in_5, in_8);
  nand A1 (A1_out, A, A);
  nand nand_2 (nand_2_out, in_1, nand_1_out);
  nand nand_3 (nand_3_out, nand_1_out, in_2);
  nand A2 (A2_out, A, A1_out);
  nand A3 (A3_out, A1_out, A);
  not not_1 (not_1_out, 1'b0);
  not not_2 (not_2_out, 1'b1);
  not not_3 (not_3_out, 1'b1);
  not not_4 (not_4_out, 1'b1);
  not not_5 (not_5_out, 1'b1);
  not not_6 (not_6_out, 1'b0);
  not not_7 (not_7_out, 1'b0);
  not not_8 (not_8_out, 1'b0);
  xor xor_2 (out_16, xor_1_out, in_9);
  and and_1 (and_1_out, in_5, in_5);
  not A4 (A4_out, A2_out);  // NAND_Gate
  Multiplexer multiplexer_2 (.in0(1'b0), .in1(not_1_out), .out(multiplexer_2_out), .sel(1'b1));  // open: en
  Multiplexer multiplexer_3 (.in0(1'b1), .in1(not_2_out), .out(multiplexer_3_out), .sel(1'b1));  // open: en
  Multiplexer multiplexer_4 (.in0(1'b1), .in1(not_3_out), .out(multiplexer_4_out), .sel(1'b1));  // open: en
  Multiplexer multiplexer_5 (.in0(1'b1), .in1(not_4_out), .out(multiplexer_5_out), .sel(1'b1));  // open: en
  Multiplexer multiplexer_6 (.in0(1'b1), .in1(not_5_out), .out(multiplexer_6_out), .sel(1'b1));  // open: en
  Multiplexer multiplexer_7 (.in0(1'b0), .in1(not_6_out), .out(multiplexer_7_out), .sel(1'b1));  // open: en
  Multiplexer multiplexer_8 (.in0(1'b0), .in1(not_7_out), .out(multiplexer_8_out), .sel(1'b1));  // open: en
  Multiplexer multiplexer_9 (.in0(1'b0), .in1(not_8_out), .out(multiplexer_9_out), .sel(1'b1));  // open: en
  nand nand_4 (out_13, nand_2_out, nand_2_out, nand_3_out);
  and and_2 (and_2_out, xor_1_out, in_9);
  Adder #(.width(1)) adder_1 (.a(1'b1), .b(multiplexer_2_out), .out(out_20), .cin(1'b1), .cout(out_21));
  Adder #(.width(1)) adder_2 (.a(1'b0), .b(multiplexer_3_out), .out(out_23), .cin(out_21), .cout(out_24));
  Adder #(.width(1)) adder_3 (.a(1'b1), .b(multiplexer_4_out), .out(out_25), .cin(out_24), .cout(out_26));
  Adder #(.width(1)) adder_4 (.a(1'b0), .b(multiplexer_5_out), .out(out_27), .cin(out_26), .cout(out_28));
  Adder #(.width(1)) adder_5 (.a(1'b1), .b(multiplexer_6_out), .out(out_29), .cin(out_28), .cout(out_30));
  Adder #(.width(1)) adder_6 (.a(1'b0), .b(multiplexer_7_out), .out(out_31), .cin(out_30), .cout(out_32));
  Adder #(.width(1)) adder_7 (.a(1'b1), .b(multiplexer_8_out), .out(out_33), .cin(out_32), .cout(out_34));
  Adder #(.width(1)) adder_8 (.a(1'b0), .b(multiplexer_9_out), .out(out_35), .cin(out_34), .cout(out_36));
  or or_1 (out_17, and_2_out, and_1_out);
  nand A5 (A5_out, A4_out, A);
  nand nand_5 (nand_5_out, in_3, in_4);
  nand nand_6 (nand_6_out, in_6, in_6);
  nand nand_7 (nand_7_out, in_7, in_7);
  not A6 (A6_out, A5_out);  // NAND_Gate
  nand A7 (A7_out, A5_out, A);
  nand nand_8 (out_15, nand_6_out, nand_6_out, nand_7_out, nand_7_out);
  not not_9 (not_9_out, d_ff_1_q);
  nand nand_9 (out_14, nand_5_out, nand_5_out);
  nand A8 (out_18, A6_out, A7_out);
  nand A9 (out_19, A1_out, A5_out);
  not not_10 (not_10_out, not_9_out);
  not not_11 (not_11_out, not_10_out);
  Clock clock_1 (.out(clock_1_out));
  D_Flip_Flop d_ff_1 (.clk(clock_1_out), .D(not_11_out), .Q(d_ff_1_q));  // open: Qn, preset, en, reset

  assign B = A;
  assign C = A;

  // Notes on the sheet:
  //   Sub Signal
endmodule
