// Logisim project lock2.circ as structural Verilog: 1 circuit, main circuit main
module main (
  input  X,
  output OUTPUT,
  output out_3,
  output S_prime_1,
  output out_5,
  output S_prime_0
);

  wire and_1_out, and_2_out, and_3_out, and_4_out, clock_1_out, not_1_out, not_2_out, not_3_out;

  not not_1 (not_1_out, X);
  not not_2 (not_2_out, S_prime_1);
  not not_3 (not_3_out, S_prime_0);
  and and_1 (and_1_out, X, S_prime_1, S_prime_0);
  and and_2 (and_2_out, not_1_out, not_2_out, S_prime_0);
  and and_3 (and_3_out, S_prime_1, not_1_out, not_3_out);
  and and_4 (and_4_out, not_2_out, not_3_out, X);
  or or_1 (out_3, and_2_out, and_3_out);
  or or_2 (out_5, and_4_out, and_3_out);
  Clock clock_1 (.out(clock_1_out));
  D_Flip_Flop d_ff_1 (.clk(clock_1_out), .D(and_1_out), .Q(OUTPUT));  // open: Qn, preset, en, reset
  D_Flip_Flop d_ff_2 (.clk(clock_1_out), .D(out_3), .Q(S_prime_1));  // open: Qn, preset, en, reset
  D_Flip_Flop d_ff_3 (.clk(clock_1_out), .D(out_5), .Q(S_prime_0));  // open: Qn, preset, en, reset

  // Notes on the sheet:
  //   S1
  //   S0
endmodule
