// Logisim project nand-board-2015.circ as structural Verilog: 1 circuit, main circuit main
module main (
  input  A,
  input  in_2,
  input  in_3,
  input  in_4,
  input  Q,
  input  in_6,
  input  in_7,
  input  in_8,
  input  in_9,
  input  in_10,
  input  B,
  input  in_12,
  input  in_13,
  input  in_14,
  input  in_15,
  input  in_16,
  input  in_17,
  input  in_18,
  input  in_19,
  input  in_20,
  input  in_21,
  input  in_22,
  input  in_23,
  input  in_24,
  input  in_25,
  input  in_26,
  input  in_27,
  input  in_28,
  input  in_29,
  input  in_30,
  input  in_31,
  input  in_32,
  input  in_33,
  input  in_34,
  input  in_35,
  input  in_36,
  input  in_37,
  input  in_38,
  input  in_39,
  input  in_40,
  input  in_41,
  input  in_42,
  input  in_43,
  input  in_44,
  input  in_45,
  input  in_46,
  input  in_47,
  input  in_48,
  input  in_49,
  input  in_50,
  input  Switch_pins,
  input  in_52,
  input  in_53,
  input  in_54,
  input  in_55,
  input  in_56,
  input  in_57,
  input  in_58,
  input  in_59,
  input  in_60,
  input  in_61,
  input  in_62,
  input  in_63,
  input  in_64,
  input  in_65,
  input  in_66,
  input  in_67,
  input  in_68,
  input  in_69,
  input  in_70,
  input  in_71,
  input  in_72,
  input  in_73,
  input  in_74,
  input  in_75,
  input  in_76,
  input  in_77,
  input  in_78,
  input  in_79,
  input  in_80,
  input  in_81,
  input  in_82,
  input  in_83,
  input  in_84,
  input  in_85,
  input  in_86,
  input  in_87,
  input  in_88,
  input  in_89,
  input  in_90,
  input  in_91,
  input  in_92,
  input  in_93,
  input  in_94,
  input  in_95,
  input  in_96,
  input  in_97,
  input  in_98,
  input  in_99,
  input  in_100,
  input  in_101,
  input  in_102,
  input  in_103,
  input  in_104,
  input  in_105,
  input  in_106,
  input  in_107,
  input  in_108,
  input  in_109,
  input  in_110,
  input  in_111,
  input  in_112,
  input  in_113,
  input  in_114,
  input  in_115,
  input  in_116,
  input  in_117,
  input  in_118,
  input  in_119,
  input  in_120,
  input  in_121,
  input  in_122,
  input  in_123,
  input  in_124,
  input  in_125,
  input  in_126,
  input  in_127,
  input  in_128,
  input  in_129,
  input  in_130,
  input  in_131,
  input  in_132,
  input  in_133,
  input  in_134,
  input  in_135,
  input  in_136,
  input  in_137,
  input  in_138,
  input  in_139,
  input  in_140,
  input  in_141,
  input  in_142,
  input  in_143,
  input  in_144,
  input  in_145,
  input  in_146,
  input  in_147,
  input  in_148,
  input  in_149,
  input  in_150,
  input  in_151,
  input  in_152,
  input  in_153,
  input  in_154,
  input  in_155,
  input  in_156,
  input  in_157,
  input  in_158,
  input  in_159,
  input  in_160,
  input  in_161,
  input  in_162,
  input  in_163,
  input  in_164,
  input  in_165,
  input  in_166,
  input  in_167,
  input  in_168,
  input  in_169,
  input  in_170,
  input  in_171,
  input  in_172,
  input  in_173,
  input  in_174,
  input  in_175,
  input  in_176
);

  // Probe on A
  Pull_Resistor pull_resistor_1 (.node(A));
  Pull_Resistor pull_resistor_2 (.node(A));
  Pull_Resistor pull_resistor_3 (.node(in_22));
  Pull_Resistor pull_resistor_4 (.node(in_32));
  Pull_Resistor pull_resistor_5 (.node(in_42));
  Pull_Resistor pull_resistor_6 (.node(in_54));
  Pull_Resistor pull_resistor_7 (.node(in_66));
  Pull_Resistor pull_resistor_8 (.node(in_78));
  Pull_Resistor pull_resistor_9 (.node(in_94));
  Pull_Resistor pull_resistor_10 (.node(in_106));
  Pull_Resistor pull_resistor_11 (.node(in_118));
  Pull_Resistor pull_resistor_12 (.node(in_128));
  Pull_Resistor pull_resistor_13 (.node(in_138));
  Pull_Resistor pull_resistor_14 (.node(in_148));
  Pull_Resistor pull_resistor_15 (.node(in_158));
  Pull_Resistor pull_resistor_16 (.node(in_168));
  nand nand_1 (in_4, A, A);
  nand nand_2 (in_24, in_22, in_32);
  nand nand_3 (in_44, in_42, in_54);
  nand nand_4 (in_68, in_66, in_78);
  nand nand_5 (in_96, in_94, in_106);
  nand nand_6 (in_120, in_118, in_128);
  nand nand_7 (in_140, in_138, in_148);
  nand nand_8 (in_160, in_158, in_168);
  LED led_1 (.in(in_4));
  LED led_2 (.in(in_24));
  LED led_3 (.in(in_44));
  LED led_4 (.in(in_68));
  LED led_5 (.in(in_96));
  LED led_6 (.in(in_120));
  LED led_7 (.in(in_140));
  LED led_8 (.in(in_160));
  Pull_Resistor pull_resistor_17 (.node(in_7));
  Pull_Resistor pull_resistor_18 (.node(in_17));
  Pull_Resistor pull_resistor_19 (.node(in_27));
  Pull_Resistor pull_resistor_20 (.node(in_37));
  Pull_Resistor pull_resistor_21 (.node(in_47));
  Pull_Resistor pull_resistor_22 (.node(in_59));
  Pull_Resistor pull_resistor_23 (.node(in_71));
  Pull_Resistor pull_resistor_24 (.node(in_83));
  Pull_Resistor pull_resistor_25 (.node(in_99));
  Pull_Resistor pull_resistor_26 (.node(in_111));
  Pull_Resistor pull_resistor_27 (.node(in_123));
  Pull_Resistor pull_resistor_28 (.node(in_133));
  Pull_Resistor pull_resistor_29 (.node(in_143));
  Pull_Resistor pull_resistor_30 (.node(in_153));
  Pull_Resistor pull_resistor_31 (.node(in_163));
  Pull_Resistor pull_resistor_32 (.node(in_173));
  nand nand_9 (in_9, in_7, in_17);
  nand nand_10 (in_29, in_27, in_37);
  nand nand_11 (in_49, in_47, in_59);
  nand nand_12 (in_73, in_71, in_83);
  nand nand_13 (in_101, in_99, in_111);
  nand nand_14 (in_125, in_123, in_133);
  nand nand_15 (in_145, in_143, in_153);
  nand nand_16 (in_165, in_163, in_173);
  LED led_9 (.in(in_9));
  LED led_10 (.in(in_29));
  LED led_11 (.in(in_49));
  LED led_12 (.in(in_73));
  LED led_13 (.in(in_101));
  LED led_14 (.in(in_125));
  LED led_15 (.in(in_145));
  LED led_16 (.in(in_165));

  assign B = A;
  assign in_2 = A;
  assign in_3 = A;
  assign in_6 = A;
  assign in_8 = in_7;
  assign in_10 = in_9;
  assign in_12 = A;
  assign in_13 = A;
  assign in_14 = in_4;
  assign in_15 = in_4;
  assign in_16 = A;
  assign in_18 = in_17;
  assign in_19 = in_9;
  assign in_20 = in_9;
  assign in_21 = A;
  assign in_23 = in_22;
  assign in_25 = in_24;
  assign in_26 = A;
  assign in_28 = in_27;
  assign in_30 = in_29;
  assign in_31 = A;
  assign in_33 = in_32;
  assign in_34 = in_24;
  assign in_35 = in_24;
  assign in_36 = A;
  assign in_38 = in_37;
  assign in_39 = in_29;
  assign in_40 = in_29;
  assign in_41 = A;
  assign in_43 = in_42;
  assign in_45 = in_44;
  assign in_46 = A;
  assign in_48 = in_47;
  assign in_50 = in_49;
  assign in_53 = A;
  assign in_55 = in_54;
  assign in_56 = in_44;
  assign in_57 = in_44;
  assign in_58 = A;
  assign in_60 = in_59;
  assign in_61 = in_49;
  assign in_62 = in_49;
  assign in_63 = in_52;
  assign in_64 = in_52;
  assign in_65 = A;
  assign in_67 = in_66;
  assign in_69 = in_68;
  assign in_70 = A;
  assign in_72 = in_71;
  assign in_74 = in_73;
  assign in_76 = in_75;
  assign in_77 = A;
  assign in_79 = in_78;
  assign in_80 = in_68;
  assign in_81 = in_68;
  assign in_82 = A;
  assign in_84 = in_83;
  assign in_85 = in_73;
  assign in_86 = in_73;
  assign in_87 = in_75;
  assign in_88 = in_75;
  assign in_90 = in_89;
  assign in_91 = in_89;
  assign in_92 = in_89;
  assign in_93 = A;
  assign in_95 = in_94;
  assign in_97 = in_96;
  assign in_98 = A;
  assign in_100 = in_99;
  assign in_102 = in_101;
  assign in_104 = in_103;
  assign in_105 = A;
  assign in_107 = in_106;
  assign in_108 = in_96;
  assign in_109 = in_96;
  assign in_110 = A;
  assign in_112 = in_111;
  assign in_113 = in_101;
  assign in_114 = in_101;
  assign in_115 = in_103;
  assign in_116 = in_103;
  assign in_117 = A;
  assign in_119 = in_118;
  assign in_121 = in_120;
  assign in_122 = A;
  assign in_124 = in_123;
  assign in_126 = in_125;
  assign in_127 = A;
  assign in_129 = in_128;
  assign in_130 = in_120;
  assign in_131 = in_120;
  assign in_132 = A;
  assign in_134 = in_133;
  assign in_135 = in_125;
  assign in_136 = in_125;
  assign in_137 = A;
  assign in_139 = in_138;
  assign in_141 = in_140;
  assign in_142 = A;
  assign in_144 = in_143;
  assign in_146 = in_145;
  assign in_147 = A;
  assign in_149 = in_148;
  assign in_150 = in_140;
  assign in_151 = in_140;
  assign in_152 = A;
  assign in_154 = in_153;
  assign in_155 = in_145;
  assign in_156 = in_145;
  assign in_157 = A;
  assign in_159 = in_158;
  assign in_161 = in_160;
  assign in_162 = A;
  assign in_164 = in_163;
  assign in_166 = in_165;
  assign in_167 = A;
  assign in_169 = in_168;
  assign in_170 = in_160;
  assign in_171 = in_160;
  assign in_172 = A;
  assign in_174 = in_173;
  assign in_175 = in_165;
  assign in_176 = in_165;
  assign Q = in_4;
  assign Switch_pins = in_52;
  // also tied to GND on the sheet: {in_75, in_89, in_103, in_52}
  // also tied to VCC on the sheet: A

  // Notes on the sheet:
  //   Switches
  //   Constant '1' pins
endmodule
