// Logisim project vending machine.circ as structural Verilog: 1 circuit, main circuit main
module main (
  output Y1,
  output Y0,
  output out_3,
  output out_4,
  output Y1_2,
  output Y0_2,
  output S1_prime,
  output S0_prime
);

  wire and_1_out, and_2_out, and_3_out, and_4_out, and_5_out, and_6_out, and_7_out, and_8_out, and_9_out,
       and_10_out, and_11_out, and_12_out, and_13_out, and_14_out, and_16_out, clock_1_out, clock_2_out,
       d_ff_1_q, d_ff_2_q, not_1_out, not_2_out, not_3_out, not_4_out, not_5_out, not_6_out, not_7_out,
       not_8_out, or_3_out, or_4_out, or_6_out;

  Clock clock_1 (.out(clock_1_out));
  D_Flip_Flop d_ff_1 (.clk(clock_1_out), .D(out_3), .Q(d_ff_1_q));  // open: Qn, preset, en, reset
  D_Flip_Flop d_ff_2 (.clk(clock_1_out), .D(out_4), .Q(d_ff_2_q));  // open: Qn, preset, en, reset
  not not_1 (not_1_out, d_ff_1_q);
  not not_2 (not_2_out, d_ff_2_q);
  not not_3 (not_3_out, 1'b1);
  not not_4 (not_4_out, 1'b0);
  not not_5 (not_5_out, S1_prime);
  not not_6 (not_6_out, S0_prime);
  not not_7 (not_7_out, 1'b1);
  not not_8 (not_8_out, 1'b0);
  and and_1 (and_1_out, not_1_out, d_ff_2_q, 1'b1, not_4_out);
  and and_2 (and_2_out, not_5_out, S0_prime, 1'b1, not_8_out);
  and and_3 (and_3_out, d_ff_1_q, not_2_out, not_3_out, 1'b0);
  and and_4 (and_4_out, not_1_out, d_ff_2_q, not_3_out, 1'b0);
  and and_5 (and_5_out, S1_prime, not_6_out, not_7_out, 1'b0);
  and and_6 (and_6_out, not_5_out, S0_prime, not_7_out, 1'b0);
  and and_7 (and_7_out, not_1_out, not_2_out, 1'b1, not_4_out);
  and and_8 (and_8_out, d_ff_1_q, not_2_out, not_3_out, not_4_out);
  and and_9 (and_9_out, not_1_out, not_2_out, not_3_out, 1'b0);
  and and_10 (and_10_out, not_1_out, d_ff_2_q, not_3_out, not_4_out);
  and and_11 (and_11_out, not_5_out, not_6_out, 1'b1, not_8_out);
  and and_12 (and_12_out, S1_prime, not_6_out, not_7_out, not_8_out);
  and and_13 (and_13_out, not_5_out, not_6_out, not_7_out, 1'b0);
  and and_14 (and_14_out, not_5_out, S0_prime, not_7_out, not_8_out);
  or or_1 (out_3, and_7_out, and_4_out, and_8_out);
  or or_2 (out_4, and_9_out, and_10_out);
  or or_3 (or_3_out, and_11_out, and_6_out, and_12_out);
  or or_4 (or_4_out, and_13_out, and_14_out);
  and and_15 (Y1, d_ff_1_q, not_2_out, 1'b1, not_4_out);
  and and_16 (and_16_out, S1_prime, not_6_out, 1'b1, not_8_out);
  or or_5 (Y0, Y1, and_3_out, and_1_out);
  Clock clock_2 (.out(clock_2_out));
  or or_6 (or_6_out, and_16_out, and_5_out, and_2_out);
  D_Flip_Flop d_ff_3 (.clk(clock_2_out), .D(and_16_out), .Q(Y1_2));  // open: Qn, preset, en, reset
  D_Flip_Flop d_ff_4 (.clk(clock_2_out), .D(or_6_out), .Q(Y0_2));  // open: Qn, preset, en, reset
  D_Flip_Flop d_ff_5 (.clk(clock_2_out), .D(or_3_out), .Q(S1_prime));  // open: Qn, preset, en, reset
  D_Flip_Flop d_ff_6 (.clk(clock_2_out), .D(or_4_out), .Q(S0_prime));  // open: Qn, preset, en, reset

  // Notes on the sheet:
  //   S1
  //   S0
  //   A
  //   B
  //   S1
  //   S0
  //   A
  //   B
  //   S1'
  //   S0'
endmodule
