// Logisim project fromnandtoothergates.circ as structural Verilog: 1 circuit, main circuit main
module main (
  input  in_1,
  input  in_2,
  input  in_3,
  input  in_4,
  input  in_5,
  input  in_6,
  input  in_7,
  input  in_8,
  input  in_9,
  input  full_adder,
  input  in_11,
  input  in_12,
  output out_13,
  output out_14,
  output out_15,
  output out_16,
  output out_17,
  output out_18,
  output out_19,
  output out_20,
  output out_21,
  output out_22,
  output out_23,
  output out_24,
  output out_25,
  output out_26,
  output out_27
);

  wire and_2_out, and_3_out, nand_1_out, nand_2_out, nand_3_out, nand_4_out, nand_5_out, nand_6_out,
       nand_9_out, nand_10_out, nand_11_out, nand_12_out, nand_13_out, nand_14_out, nand_15_out, nand_16_out,
       nand_17_out, nand_18_out, nand_24_out, nand_25_out, nand_26_out, nand_30_out, xor_1_out;

  nand nand_1 (nand_1_out, in_7, in_9);
  nand nand_2 (nand_2_out, 1'b1, 1'b0);
  ExactlyOne xor_1 (.out(xor_1_out), .in1(full_adder), .in3(in_11), .in4(in_11));
  nand nand_3 (nand_3_out, 1'b1, nand_2_out);
  nand nand_4 (nand_4_out, nand_2_out, 1'b0);
  xor xor_2 (out_13, in_2, in_3);
  and and_1 (out_15, in_2, in_2, in_3, in_3);
  nand nand_5 (nand_5_out, in_7, nand_1_out);
  nand nand_6 (nand_6_out, nand_1_out, in_9);
  and and_2 (and_2_out, xor_1_out, in_12);
  and and_3 (and_3_out, full_adder, in_11);
  nand nand_7 (out_25, nand_3_out, nand_4_out);
  nand nand_8 (out_19, nand_5_out, nand_6_out);
  ExactlyOne xor_3 (.out(out_22), .in1(xor_1_out), .in3(in_12), .in4(in_12));
  nand nand_9 (nand_9_out, 1'b0, 1'b0, 1'b0);
  nand nand_10 (nand_10_out, 1'b0, 1'b0);
  or or_1 (out_23, and_2_out, and_3_out, and_3_out);
  nand nand_11 (nand_11_out, 1'b0, 1'b0);
  nand nand_12 (nand_12_out, 1'b1, 1'b1);
  nand nand_13 (nand_13_out, nand_9_out, nand_10_out);
  nand nand_14 (nand_14_out, 1'b0, 1'b0);
  nand nand_15 (nand_15_out, 1'b0, 1'b0);
  nand nand_16 (nand_16_out, 1'b1, nand_11_out);
  nand nand_17 (nand_17_out, nand_12_out, nand_12_out, 1'b0);
  nand nand_18 (nand_18_out, 1'b0, 1'b0);
  nand nand_19 (out_26, nand_16_out, nand_16_out, nand_17_out);
  nand nand_20 (out_27, nand_13_out, nand_13_out);
  nand nand_21 (out_14, in_1, in_1);
  nand nand_22 (out_16, in_4, in_4, in_6);
  nand nand_23 (out_20, in_4, in_6);
  nand nand_24 (nand_24_out, 1'b0, 1'b0, 1'b0);
  nand nand_25 (nand_25_out, 1'b1, 1'b1, 1'b1);
  nand nand_26 (nand_26_out, nand_14_out, nand_14_out, nand_15_out, nand_15_out);
  nand nand_27 (out_18, out_16, out_20);
  nand nand_28 (out_21, nand_24_out, nand_25_out);
  nand nand_29 (out_24, nand_18_out, nand_26_out);
  nand nand_30 (nand_30_out, in_5, in_5, in_8, in_8);
  nand nand_31 (out_17, nand_30_out, nand_30_out);

  // Notes on the sheet:
  //   half adder
  //   from nand to xor
  //   from nand to nor
  //   from nand to xor
  //   from nand to or
  //   from nand to xnor
  //   from nand to and
  //   from nand to not
endmodule
