// Logisim project jk-ff-template-new.circ as structural Verilog: 1 circuit, main circuit main
module main (
  output out_1,
  output out_2
);

  wire clock_1_out, multiplexer_1_out, multiplexer_2_out, multiplexer_3_out, multiplexer_4_out, nand_1_out,
       nand_2_out, nand_3_out, nand_4_out, nand_5_out, nand_6_out, undriven;

  Clock clock_1 (.out(clock_1_out));
  Multiplexer multiplexer_1 (.in0(out_2), .in1(1'b0), .out(multiplexer_1_out), .sel(1'b1));  // open: en
  Multiplexer multiplexer_2 (.in0(1'b1), .in1(1'b0), .out(multiplexer_2_out), .sel(1'b1));  // open: en
  Multiplexer multiplexer_3 (.in0(1'b0), .in1(1'b1), .out(multiplexer_3_out), .sel(1'b1));  // open: en
  Multiplexer multiplexer_4 (.in0(out_1), .in1(1'b1), .out(multiplexer_4_out), .sel(1'b1));  // open: en
  Multiplexer #(.select(3)) multiplexer_5 (.en(undriven));  // open: in0, in1, in2, in3, in4, in5, in6, in7, out, sel
  nand nand_1 (nand_1_out, multiplexer_1_out, clock_1_out, multiplexer_2_out);
  nand nand_2 (nand_2_out, multiplexer_3_out, clock_1_out, multiplexer_4_out);
  nand nand_3 (nand_3_out, nand_1_out, nand_4_out);
  nand nand_4 (nand_4_out, nand_3_out, nand_2_out);
  nand nand_5 (nand_5_out, nand_3_out, clock_1_out);
  nand nand_6 (nand_6_out, nand_5_out, clock_1_out);
  nand nand_7 (out_1, nand_5_out, out_2);
  nand nand_8 (out_2, out_1, nand_6_out);

  // Notes on the sheet:
  //   J
  //   Clock
  //   K
  //   Reset'
  //   Feedback X
  //   Feedback Y
endmodule
