// Logisim project jk-flip-flop-waveform-question-template.circ as structural Verilog: 1 circuit, main circuit main
module main (
  input  in_1,
  input  in_2
);

  wire Clock_out, nand_1_out, nand_2_out, nand_3_out, nand_4_out, nand_5_out, nand_6_out, nand_7_out,
       nand_8_out;

  Clock Clock (.out(Clock_out));
  nand nand_1 (nand_1_out, nand_4_out, in_1, Clock_out);
  nand nand_2 (nand_2_out, Clock_out, in_2, nand_3_out);
  nand nand_3 (nand_3_out, nand_1_out, nand_4_out);
  nand nand_4 (nand_4_out, nand_3_out, nand_2_out);
  nand nand_5 (nand_5_out, nand_8_out, nand_3_out, Clock_out);
  nand nand_6 (nand_6_out, Clock_out, nand_4_out, nand_7_out);
  nand nand_7 (nand_7_out, nand_5_out, nand_8_out);
  nand nand_8 (nand_8_out, nand_7_out, nand_6_out);
  // Probe on nand_7_out

  // Notes on the sheet:
  //   Do not delete the clock and the probe components.
  //   Do not change any property of these two components.
  //   Do not add any new clock or probe components.
endmodule
