// Logisim project mux from nand.circ as structural Verilog: 1 circuit, main circuit main
module main (
  output out_1,
  output out_2,
  output out_3,
  output out_4,
  output out_5
);

  wire and_1_out, and_2_out, nand_1_out, nand_2_out, nand_3_out, nand_4_out, nand_6_out, nand_7_out,
       not_1_out;

  not not_1 (not_1_out, 1'b0);
  and and_1 (and_1_out, not_1_out, 1'b1);
  and and_2 (and_2_out, 1'b0, 1'b1);
  or or_1 (out_3, and_2_out, and_1_out);
  nand nand_1 (nand_1_out, 1'b1, 1'b1);
  nand nand_2 (nand_2_out, 1'b0, 1'b0);
  nand nand_3 (nand_3_out, 1'b1, 1'b1);
  nand nand_4 (nand_4_out, 1'b1, 1'b0);
  nand nand_5 (out_2, nand_2_out, nand_3_out);
  nand nand_6 (nand_6_out, nand_1_out, 1'b1);
  nand nand_7 (nand_7_out, 1'b1, 1'b1);
  nand nand_8 (out_1, nand_7_out, nand_7_out);
  nand nand_9 (out_4, 1'b0, 1'b0);
  nand nand_10 (out_5, nand_4_out, nand_6_out);

  // Notes on the sheet:
  //   S
  //   A
  //   B
endmodule
