// Logisim project shift register.circ as structural Verilog: 2 circuits, main circuit main
module main (
  input  D,
  input  E,
  output out_3,
  output out_4
);

  wire nand_1_out, nand_2_out, nand_3_out, nand_4_out, nand_5_out, nand_6_out, nand_7_out;

  nand nand_1 (nand_1_out, D, E);
  nand nand_2 (nand_2_out, nand_1_out, E);
  nand nand_3 (nand_3_out, E, E);
  nand nand_4 (nand_4_out, nand_1_out, nand_5_out);
  nand nand_5 (nand_5_out, nand_4_out, nand_2_out);
  nand nand_6 (nand_6_out, nand_4_out, nand_3_out);
  nand nand_7 (nand_7_out, nand_6_out, nand_3_out);
  nand nand_8 (out_3, nand_6_out, out_4);
  nand nand_9 (out_4, out_3, nand_7_out);
endmodule

module D_ff (
  output out_1,
  output out_2
);

  wire clock_1_out, main_1_out_3, main_2_out_3;

  Clock clock_1 (.out(clock_1_out));
  main main_1 (.D(1'b1), .E(clock_1_out), .out_3(main_1_out_3));  // open: out_4
  main main_2 (.D(main_1_out_3), .E(clock_1_out), .out_3(main_2_out_3));  // open: out_4
  main main_3 (.D(main_2_out_3), .E(clock_1_out), .out_3(out_1), .out_4(out_2));
endmodule
