// Logisim project subtractor.circ as structural Verilog: 1 circuit, main circuit main
module main (
  output out_1,
  output out_2,
  output out_3,
  output out_4,
  output out_5,
  output out_6,
  output out_7,
  output out_8
);

  wire adder_1_cout, adder_2_cout, adder_3_cout, adder_4_cout, adder_5_cout, adder_6_cout, adder_7_cout;

  Adder #(.width(1)) adder_1 (.a(1'b1), .b(1'b1), .out(out_1), .cin(1'b1), .cout(adder_1_cout));
  Adder #(.width(1)) adder_2 (.a(1'b1), .b(1'b1), .out(out_2), .cin(adder_1_cout), .cout(adder_2_cout));
  Adder #(.width(1)) adder_3 (.a(1'b1), .b(1'b1), .out(out_3), .cin(adder_2_cout), .cout(adder_3_cout));
  Adder #(.width(1)) adder_4 (.a(1'b1), .b(1'b1), .out(out_4), .cin(adder_3_cout), .cout(adder_4_cout));
  Adder #(.width(1)) adder_5 (.a(1'b1), .b(1'b1), .out(out_5), .cin(adder_4_cout), .cout(adder_5_cout));
  Adder #(.width(1)) adder_6 (.a(1'b1), .b(1'b1), .out(out_6), .cin(adder_5_cout), .cout(adder_6_cout));
  Adder #(.width(1)) adder_7 (.a(1'b1), .b(1'b1), .out(out_7), .cin(adder_6_cout), .cout(adder_7_cout));
  Adder #(.width(1)) adder_8 (.a(1'b1), .b(1'b1), .out(out_8), .cin(adder_7_cout));  // open: cout
endmodule
