// Logisim project three-bit counter.circ as structural Verilog: 1 circuit, main circuit main
module main (
  input  in_1,
  input  in_2,
  input  A,
  output out_4,
  output [2:0] out_5
);

  wire and_1_out, and_2_out, and_3_out, and_4_out, and_5_out, and_6_out, and_7_out, and_8_out, clock_1_out,
       d_ff_1_q, d_ff_2_q, d_ff_3_q, d_ff_4_q, not_1_out, not_2_out, not_3_out, not_4_out, not_5_out,
       not_6_out;

  Clock clock_1 (.out(clock_1_out));
  D_Flip_Flop d_ff_1 (.clk(clock_1_out), .D(out_5[0]), .Q(d_ff_1_q));  // open: Qn, preset, en, reset
  D_Flip_Flop d_ff_2 (.clk(clock_1_out), .D(out_5[1]), .Q(d_ff_2_q));  // open: Qn, preset, en, reset
  not not_1 (not_1_out, d_ff_1_q);
  not not_2 (not_2_out, A);
  not not_3 (not_3_out, d_ff_1_q);
  D_Flip_Flop d_ff_3 (.clk(clock_1_out), .D(out_5[2]), .Q(d_ff_3_q));  // open: Qn, preset, en, reset
  not not_4 (not_4_out, d_ff_2_q);
  and and_1 (and_1_out, d_ff_3_q, not_4_out);
  not not_5 (not_5_out, d_ff_3_q);
  not not_6 (not_6_out, d_ff_2_q);
  and and_2 (and_2_out, d_ff_3_q, not_1_out);
  and and_3 (and_3_out, d_ff_3_q, d_ff_1_q, not_3_out);
  and and_4 (and_4_out, not_5_out, d_ff_2_q, d_ff_1_q, A);
  and and_5 (and_5_out, not_6_out, A, d_ff_1_q);
  and and_6 (and_6_out, d_ff_2_q, A, not_3_out);
  and and_7 (and_7_out, not_3_out, not_2_out, d_ff_2_q);
  and and_8 (and_8_out, d_ff_2_q, not_2_out, d_ff_1_q);
  xor xor_1 (out_5[0], d_ff_1_q, A);
  or or_1 (out_5[2], and_1_out, and_2_out, and_3_out, and_4_out);
  or or_2 (out_5[1], and_5_out, and_6_out, and_7_out, and_8_out);
  D_Flip_Flop d_ff_4 (.clk(in_1), .D(in_2), .Q(d_ff_4_q));  // open: Qn, preset, en, reset
  D_Flip_Flop d_ff_5 (.clk(in_1), .D(d_ff_4_q), .Q(out_4));  // open: Qn, preset, en, reset

  // Notes on the sheet:
  //   S0
  //   S2
  //   S2'
  //   S1'
  //   S0'
endmodule
